# Fritzing sketch BasicIoT (saved by Fritzing 0.8.7b)
breadboards: 1

parts:
  元件1 = Arduino Uno (Rev3)
  LCD1 = LCD screen
  LCM1602_IIC2 = LCM1602 IIC [part_number="LCM1602 IIC" chip_label="LCM1602 IIC" package="DIP (Dual Inline) [THT]"]
  J1 = Basic Servo
  KY-6 = Keyes Relay [package=THT]
  IR2 = TSOP312.., 314.. [package=THT]
  J3 = male pin header, 3 pins [form="♂ (male)"]
  Keypad4x1 = Keypad Membran 4x4
  元件2 = Thumb Joystick
  J2 = Basic Servo

nets:
  N1: 元件1.A0, 元件2.VERT
  N2: 元件1.A1, 元件2.HORZ
  N3: 元件1.A2, J2.pulse
  N4: 元件1.A3, J1.pulse
  N5: 元件1.A4/SDA, LCM1602_IIC2.SDA
  N6: 元件1.A5/SCL, LCM1602_IIC2.SCL
  N7: 元件1.D8, Keypad4x1.Pin6
  N8: 元件1.D9_PWM, Keypad4x1.Pin5
  N9: 元件1.D10_PWM/SS, Keypad4x1.Pin4
  N10: 元件1.D11_PWM/MOSI, Keypad4x1.Pin3
  N11: 元件1.D12/MISO, Keypad4x1.Pin2
  N12: 元件1.D13/SCK, Keypad4x1.Pin1
  GND: 元件1.GND, LCM1602_IIC2.GND, J1.gnd, KY-6.ground, IR2.Vs, J3.pin3, 元件2.GND, J2.gnd
  N13: 元件1.D2, J3.pin2
  N14: 元件1.D3_PWM, 元件2.SEL
  N15: 元件1.D4, IR2.GND
  N16: 元件1.D5_PWM, KY-6.signal
  N17: 元件1.D6_PWM, Keypad4x1.Pin8
  N18: 元件1.D7, Keypad4x1.Pin7
  VCC: 元件1.5V, LCM1602_IIC2.VCC, J1.vcc, IR2.Data, J3.pin1, 元件2.VCC, J2.vcc
  VSS: LCD1.VSS, LCM1602_IIC2.VSS
  VDD: LCD1.VDD, LCM1602_IIC2.VDD
  N19: LCD1.V0, LCM1602_IIC2.V0
  N20: LCD1.RS, LCM1602_IIC2.RS
  N21: LCD1.R/W, LCM1602_IIC2.RW
  N22: LCD1.E, LCM1602_IIC2.E
  N23: LCD1.DB0, LCM1602_IIC2.D0
  N24: LCD1.DB1, LCM1602_IIC2.D1
  N25: LCD1.DB2, LCM1602_IIC2.D2
  N26: LCD1.DB3, LCM1602_IIC2.D3
  N27: LCD1.DB4, LCM1602_IIC2.D4
  N28: LCD1.DB5, LCM1602_IIC2.D5
  N29: LCD1.DB6, LCM1602_IIC2.D6
  N30: LCD1.DB7, LCM1602_IIC2.D7
  N31: LCD1.LED+, LCM1602_IIC2.A
  N32: LCD1.LED-, LCM1602_IIC2.K
  N33: LCM1602_IIC2.LED_A, LCM1602_IIC2.LED_B

custom parts:
  LCM1602 IIC: I2C-Module to use a 1602 or 2004 LCD on with the wire.h libory Serial LCD Modul
  Keyes Relay: The Keyes 5V relay module is suitable for SCM development, home appliance control. It uses a 5V~12V TIL control signal which can control DC / AC signal.
  Keypad Membran 4x4: Membrane Keypad 4x4 Matrix
